# Fritzing sketch New_Ping_Fritzing (saved by Fritzing 0.9.3b)
breadboards: 1

parts:
  Part1 = Arduino Uno (Rev3)
  S1 = Pushbutton [package="[THT]"]
  HC-SR04_Sensor_1 = HC-SR04 Ultrasonic Distance Sensor
  R1 = Resistor [tolerance=±5% resistance=220 package="0805 [SMD]"]

nets:
  N1: Part1.D9_PWM, S1.Pin_1, S1.Pin_2, R1.Pin_0
  N2: Part1.D11_PWM/MOSI, HC-SR04_Sensor_1.ECHO
  N3: Part1.D12/MISO, HC-SR04_Sensor_1.TRIG
  5V: Part1.5V, S1.Pin_3, S1.Pin_4, HC-SR04_Sensor_1.VCC
  GND: Part1.GND, HC-SR04_Sensor_1.GND, R1.Pin_1
